# Fritzing sketch Magic Knock (saved by Fritzing 0.9.2b)
breadboards: 1

parts:
  Part1 = Arduino Nano (Rev3.0)
  J1 = Piezo Speaker
  J2 = Basic Servo
  R1 = Resistor [tolerance=±5% resistance=1M package=THT]

nets (from the schematic view):
  N1: Part1.GND, R1.Pin_0
  N2: Part1.D9, J2.pulse
  VIN: Part1.VIN, J2.vcc
  N3: Part1.A0, J1.pin2, R1.Pin_1
